// Logisim project Nmos.circ as structural Verilog: 5 circuits, main circuit main
module main (
  input  in_1,
  input  in_2,
  input  in_3,
  input  in_4,
  input  in_5,
  input  in_6,
  input  in_7,
  input  in_8,
  input  in_9,
  output out_10,
  output out_11,
  output out_12,
  output out_13,
  output out_14
);

  wire pull_resistor_2_node, pull_resistor_5_node, transistor_8_out, transistor_10_out;

  Pull_Resistor #(.pull(1)) pull_resistor_1 (.node(out_10));
  Transistor #(.\type ("n")) transistor_1 (.in(1'b0), .out(out_10), .gate(in_4));
  Pull_Resistor #(.pull(1)) pull_resistor_2 (.node(pull_resistor_2_node));
  Transistor #(.\type ("n")) transistor_2 (.in(1'b0), .out(pull_resistor_2_node), .gate(in_8));
  Transistor #(.\type ("n")) transistor_3 (.in(1'b0), .out(pull_resistor_2_node), .gate(in_9));
  Transistor #(.\type ("n")) transistor_4 (.in(1'b0), .out(out_11), .gate(in_2));
  Pull_Resistor #(.pull(1)) pull_resistor_3 (.node(out_14));
  Transistor #(.\type ("n")) transistor_5 (.in(1'b0), .out(out_14), .gate(pull_resistor_2_node));
  Pull_Resistor #(.pull(1)) pull_resistor_4 (.node(out_11));
  Transistor #(.\type ("n")) transistor_6 (.in(1'b0), .out(out_11), .gate(in_3));
  Pull_Resistor #(.pull(1)) pull_resistor_5 (.node(pull_resistor_5_node));
  Transistor #(.\type ("n")) transistor_7 (.in(transistor_8_out), .out(pull_resistor_5_node), .gate(in_6));
  Transistor #(.\type ("n")) transistor_8 (.in(1'b0), .out(transistor_8_out), .gate(in_7));
  Pull_Resistor #(.pull(1)) pull_resistor_6 (.node(out_12));
  Transistor #(.\type ("n")) transistor_9 (.in(transistor_10_out), .out(out_12), .gate(in_1));
  Transistor #(.\type ("n")) transistor_10 (.in(1'b0), .out(transistor_10_out), .gate(in_5));
  Pull_Resistor #(.pull(1)) pull_resistor_7 (.node(out_13));
  Transistor #(.\type ("n")) transistor_11 (.in(1'b0), .out(out_13), .gate(pull_resistor_5_node));

  // Notes on the sheet:
  //   NOT Gate
  //   OR Gate
  //   NOR Gate
  //   AND Gate
  //   NAND Gate
endmodule

module Adder1Bit (
  input  A,
  input  B,
  input  Cin,
  output S,
  output Cout
);

  wire and_1_out, and_2_out, xor_1_out;

  xor xor_1 (xor_1_out, A, B);
  xor xor_2 (S, xor_1_out, Cin);
  and and_1 (and_1_out, A, B);
  and and_2 (and_2_out, xor_1_out, Cin);
  or or_1 (Cout, and_1_out, and_2_out);

  // Notes on the sheet:
  //   Full Adder
endmodule

module Adder4bit (
  input  [3:0] B,
  input  [3:0] A,
  input  cin1,
  output Co,
  output [3:0] Sum
);

  wire adder1bit_2_cout, adder1bit_3_cout, adder1bit_4_cout;

  Adder1Bit adder1bit_1 (.A(A[3]), .B(B[3]), .Cin(adder1bit_2_cout), .S(Sum[3]), .Cout(Co));
  Adder1Bit adder1bit_2 (.A(A[2]), .B(B[2]), .Cin(adder1bit_3_cout), .S(Sum[2]), .Cout(adder1bit_2_cout));
  Adder1Bit adder1bit_3 (.A(A[1]), .B(B[1]), .Cin(adder1bit_4_cout), .S(Sum[1]), .Cout(adder1bit_3_cout));
  Adder1Bit adder1bit_4 (.A(A[0]), .B(B[0]), .Cin(cin1), .S(Sum[0]), .Cout(adder1bit_4_cout));

  // Notes on the sheet:
  //   4BIT ADDER
endmodule

module adder4bitwithoutsplitter (
  input  A3,
  input  A2,
  input  A1,
  input  A0,
  input  B3,
  input  B2,
  input  B1,
  input  B0,
  input  Cin,
  output Cout,
  output S3,
  output S2,
  output S1,
  output S0
);

  wire adder1bit_2_cout, adder1bit_3_cout, adder1bit_4_cout;

  Adder1Bit adder1bit_1 (.A(A3), .B(B3), .Cin(adder1bit_2_cout), .S(S3), .Cout(Cout));
  Adder1Bit adder1bit_2 (.A(A2), .B(B2), .Cin(adder1bit_3_cout), .S(S2), .Cout(adder1bit_2_cout));
  Adder1Bit adder1bit_3 (.A(A1), .B(B1), .Cin(adder1bit_4_cout), .S(S1), .Cout(adder1bit_3_cout));
  Adder1Bit adder1bit_4 (.A(A0), .B(B0), .Cin(Cin), .S(S0), .Cout(adder1bit_4_cout));

  // Notes on the sheet:
  //   4BIT ADDER
endmodule

module MultipleBitAdder (
  input  [3:0] A,
  input  [3:0] B,
  input  Cin,
  output Co,
  output [3:0] S
);

  Adder4bit adder4bit_1 (.cin1(Cin), .B(B), .A(A), .Co(Co), .Sum(S));
endmodule
